# Fritzing sketch Wiring (saved by Fritzing 0.9.3b)
breadboards: 1

parts:
  Bauteil1 = Bluetooth HC-05 Macho
  Bauteil2 = Arduino Nano (Rev3.0) (ICSP)
  VCC1 = Battery block 9V
  Bauteil3 = InvenSense MPU6050
  R1 = Resistor [tolerance=±5% resistance=4.7k package=THT]
  R2 = Resistor [tolerance=±5% resistance=4.7k package=THT]
  LED3 = RGB LED (com. cathode, rbg) [package="5 mm [THT]"]  # not connected
  LED4 = RGB LED (com. cathode, rbg) [package="5 mm [THT]"]
  LED5 = RGB LED (com. cathode, rbg) [package="5 mm [THT]"]

nets:
  N1: Bauteil1.TXD, Bauteil2.D0/RX
  N2: Bauteil1.RXD, Bauteil2.D1/TX
  VCC: Bauteil1.VCC, Bauteil2.5V, R1.Pin_1, R2.Pin_1
  GND: Bauteil1.GND, Bauteil2.GND, VCC1.-, Bauteil3.GND, LED4.common_cathode, LED5.common_cathode
  N3: Bauteil2.VIN, VCC1.+
  N4: Bauteil2.A5, Bauteil3.SCL
  N5: Bauteil2.A4, Bauteil3.SDA, R1.Pin_0
  3V3: Bauteil2.3V3, Bauteil3.VCC
  N6: LED4.red_anode, LED5.red_anode
  N7: LED4.blue_anode, LED5.blue_anode
  N8: LED4.green_anode, LED5.green_anode
